# Fritzing sketch Breadboard Sketch (saved by Fritzing 0.9.3b)
breadboards: 1

parts:
  Part1 = Arduino Uno (Rev3)
  U1 = 74HC595 [package="DIP16 [THT]"]
  U2 = 74HC595 [package="DIP16 [THT]"]

nets:
  N1: Part1.D8, U1.ST_CP
  N2: Part1.D10_PWM/SS, U1.SH_CP
  N3: Part1.D11_PWM/MOSI, U1.DS
  GND: Part1.GND, U1.GND, U1.OE, U2.GND, U2.OE
  VCC: Part1.5V, U1.MR, U1.VCC, U2.MR, U2.VCC
  N4: U1.Q7', U2.DS
